# Fritzing sketch GameGirl (saved by Fritzing 0.9.3b)
breadboards: 1

parts:
  Composant1 = Arduino Nano (Rev3.0)
  VCC1 = Battery block 9V
  U1 = LCD-16X2 [package=lcd-16x2]
  U2 = PCF8574 [package="DIP16 [THT]"]
  U3 = POT [package=3362u]  # not connected
  LED5 = smd LED [color="Red (633nm)" package="1206 [SMD]"]
  LED6 = smd LED [color="Yellow (595nm)" package="1206 [SMD]"]
  LED7 = smd LED [color="Green (570nm)" package="1206 [SMD]"]
  LED8 = smd LED [color="Blue (430nm)" package="1206 [SMD]"]
  S1 = Round Pushbutton
  S2 = Round Pushbutton
  S3 = Round Pushbutton
  S4 = Round Pushbutton
  S5 = SPST Switch [package=switch-spdt]  # not connected
  J1 = Piezo Speaker

nets:
  GND: Composant1.GND, VCC1.-, U2.GND, LED8.cathode
  N1: Composant1.D2, S1.leg0
  N2: Composant1.D3, LED5.anode
  N3: Composant1.D4, S2.leg0
  N4: Composant1.D5, LED6.anode
  N5: Composant1.D6, S3.leg0
  N6: Composant1.D7, LED7.anode
  N7: Composant1.D9, LED8.anode
  N8: Composant1.D11/MOSI, J1.pin2
  5V: Composant1.5V, U2.VCC
  N9: U1.RS, U2.P0
  N10: U1.R_W, U2.P1
  N11: U1.E, U2.P2
  N12: U1.DB6, U2.P7
  N13: U1.DB7, U2.P6
  N14: U1.A, U2.P5
  N15: U1.K, U2.P4
  N16: S3.leg1, S4.leg1
